// Logisim project SomadorSubtrador5bits.circ as structural Verilog: 2 circuits, main circuit main
module main (
  input  A0,
  input  B0,
  input  CI,
  input  A1,
  input  B1,
  input  A2,
  input  B2,
  input  A3,
  input  B3,
  input  A4,
  input  in_11,
  input  B4
);

  wire and_1_out, and_2_out, and_3_out, and_4_out, and_5_out, and_6_out, and_7_out, and_8_out, and_9_out,
       and_10_out, and_11_out, and_12_out, and_13_out, and_14_out, and_15_out, and_16_out, and_17_out,
       and_18_out, and_19_out, and_20_out, and_21_out, and_22_out, and_23_out, and_24_out, and_25_out,
       and_26_out, and_27_out, and_28_out, and_29_out, and_30_out, not_1_out, not_2_out, not_3_out,
       not_4_out, not_5_out, not_6_out, not_7_out, not_8_out, not_9_out, not_10_out, not_11_out, not_12_out,
       not_13_out, not_14_out, not_15_out, not_16_out, not_17_out, not_18_out, not_19_out, not_20_out,
       not_21_out, not_22_out, not_23_out, or_1_out, or_2_out, or_3_out, or_4_out, or_5_out, or_6_out,
       or_7_out, or_8_out, or_9_out, or_10_out, or_11_out, or_12_out, or_13_out, or_14_out, or_15_out,
       or_16_out, or_17_out, or_18_out, or_19_out, or_20_out, or_21_out, or_22_out, or_23_out, or_24_out,
       or_25_out, or_26_out, xor_1_out, xor_2_out, xor_3_out, xor_4_out, xor_5_out, xor_6_out, xor_7_out,
       xor_8_out, xor_9_out, xor_10_out;

  not not_1 (not_1_out, in_11);
  not not_2 (not_2_out, A0);
  not not_3 (not_3_out, A0);
  not not_4 (not_4_out, in_11);
  _7_Segment_Display u_7_segment_display_1 (.g(in_11), .b(in_11), .e(in_11), .d(in_11), .c(in_11));  // open: f, a, dp
  xor xor_1 (xor_1_out, A0, B0);
  and and_1 (and_1_out, B0, not_1_out, CI);
  and and_2 (and_2_out, A0, not_1_out, CI);
  and and_3 (and_3_out, A0, not_1_out, B0);
  and and_4 (and_4_out, B0, in_11, CI);
  and and_5 (and_5_out, not_2_out, in_11, B0);
  and and_6 (and_6_out, not_3_out, in_11, CI);
  _7_Segment_Display u_7_segment_display_2 (
    .g(not_4_out), .f(not_4_out), .a(not_4_out), .b(in_11), .d(not_4_out), .c(or_1_out));  // open: e, dp
  or or_1 (or_1_out, not_4_out, in_11);
  or or_2 (or_2_out, and_1_out, and_2_out, and_3_out);
  or or_3 (or_3_out, and_4_out, and_5_out, and_6_out);
  not not_5 (not_5_out, in_11);
  or or_4 (or_4_out, not_5_out, in_11);
  _7_Segment_Display u_7_segment_display_3 (
    .g(in_11), .f(or_4_out), .a(in_11), .b(not_5_out), .e(or_5_out), .d(not_5_out), .c(not_5_out));  // open: dp
  or or_5 (or_5_out, not_5_out, in_11);
  xor xor_2 (xor_2_out, xor_1_out, CI);
  not not_6 (not_6_out, in_11);
  or or_6 (or_6_out, not_6_out, in_11);
  or or_7 (or_7_out, not_6_out, in_11);
  _7_Segment_Display u_7_segment_display_4 (
    .g(in_11), .f(or_6_out), .a(or_7_out), .b(not_6_out), .e(or_8_out), .c(not_6_out));  // open: d, dp
  or or_8 (or_8_out, not_6_out, in_11);
  not not_7 (not_7_out, in_11);
  not not_8 (not_8_out, A1);
  not not_9 (not_9_out, A1);
  xor xor_3 (xor_3_out, A1, B1);
  and and_7 (and_7_out, B1, not_7_out, or_2_out);
  and and_8 (and_8_out, A1, not_7_out, or_2_out);
  and and_9 (and_9_out, A1, not_7_out, B1);
  and and_10 (and_10_out, B1, in_11, or_3_out);
  and and_11 (and_11_out, not_8_out, in_11, B1);
  and and_12 (and_12_out, not_9_out, in_11, or_3_out);
  or or_9 (or_9_out, and_7_out, and_8_out, and_9_out);
  or or_10 (or_10_out, and_10_out, and_11_out, and_12_out);
  ExactlyOne xor_4 (.out(xor_4_out), .in0(xor_3_out), .in1(or_3_out), .in2(or_2_out));
  not not_10 (not_10_out, in_11);
  not not_11 (not_11_out, A2);
  not not_12 (not_12_out, A2);
  xor xor_5 (xor_5_out, A2, B2);
  and and_13 (and_13_out, B2, not_10_out, or_9_out);
  and and_14 (and_14_out, A2, not_10_out, or_9_out);
  and and_15 (and_15_out, A2, not_10_out, B2);
  and and_16 (and_16_out, B2, in_11, or_10_out);
  and and_17 (and_17_out, not_11_out, in_11, B2);
  and and_18 (and_18_out, not_12_out, in_11, or_10_out);
  or or_11 (or_11_out, and_13_out, and_14_out, and_15_out);
  or or_12 (or_12_out, and_16_out, and_17_out, and_18_out);
  ExactlyOne xor_6 (.out(xor_6_out), .in0(xor_5_out), .in1(or_10_out), .in2(or_9_out));
  not not_13 (not_13_out, in_11);
  not not_14 (not_14_out, A3);
  not not_15 (not_15_out, A3);
  xor xor_7 (xor_7_out, A3, B3);
  and and_19 (and_19_out, B3, not_13_out, or_11_out);
  and and_20 (and_20_out, A3, not_13_out, or_11_out);
  and and_21 (and_21_out, A3, not_13_out, B3);
  and and_22 (and_22_out, B3, in_11, or_12_out);
  and and_23 (and_23_out, not_14_out, in_11, B3);
  and and_24 (and_24_out, not_15_out, in_11, or_12_out);
  or or_13 (or_13_out, and_19_out, and_20_out, and_21_out);
  or or_14 (or_14_out, and_22_out, and_23_out, and_24_out);
  not not_16 (not_16_out, xor_10_out);
  _7_Segment_Display u_7_segment_display_5 (
    .f(not_16_out), .a(not_16_out), .b(or_15_out), .e(not_16_out), .d(not_16_out), .c(or_16_out));  // open: g, dp
  ExactlyOne xor_8 (.out(xor_8_out), .in0(xor_7_out), .in1(or_12_out), .in2(or_11_out));
  or or_15 (or_15_out, not_16_out, xor_10_out);
  or or_16 (or_16_out, not_16_out, xor_10_out);
  not not_17 (not_17_out, xor_8_out);
  or or_17 (or_17_out, not_17_out, xor_8_out);
  _7_Segment_Display u_7_segment_display_6 (
    .f(not_17_out), .a(not_17_out), .b(or_17_out), .e(not_17_out), .d(not_17_out), .c(or_18_out));  // open: g, dp
  or or_18 (or_18_out, not_17_out, xor_8_out);
  not not_18 (not_18_out, in_11);
  not not_19 (not_19_out, xor_6_out);
  _7_Segment_Display u_7_segment_display_7 (
    .f(not_19_out), .a(not_19_out), .b(or_20_out), .e(not_19_out), .d(not_19_out), .c(or_19_out));  // open: g, dp
  or or_19 (or_19_out, not_19_out, xor_6_out);
  and and_25 (and_25_out, B4, not_18_out, or_13_out);
  and and_26 (and_26_out, A4, not_18_out, or_13_out);
  and and_27 (and_27_out, A4, not_18_out, B4);
  and and_28 (and_28_out, B4, in_11, or_14_out);
  not not_20 (not_20_out, A4);
  and and_29 (and_29_out, not_20_out, in_11, B4);
  not not_21 (not_21_out, A4);
  and and_30 (and_30_out, not_21_out, in_11, or_14_out);
  not not_22 (not_22_out, xor_4_out);
  or or_20 (or_20_out, not_19_out, xor_6_out);
  xor xor_9 (xor_9_out, A4, B4);
  or or_21 (or_21_out, and_25_out, and_26_out, and_27_out);
  or or_22 (or_22_out, and_28_out, and_29_out, and_30_out);
  or or_23 (or_23_out, not_22_out, xor_4_out);
  _7_Segment_Display u_7_segment_display_8 (
    .f(not_22_out), .a(not_22_out), .b(or_23_out), .e(not_22_out), .d(not_22_out), .c(or_24_out));  // open: g, dp
  or or_24 (or_24_out, not_22_out, xor_4_out);
  ExactlyOne xor_10 (.out(xor_10_out), .in0(xor_9_out), .in1(or_14_out), .in2(or_13_out));
  not not_23 (not_23_out, xor_2_out);
  _7_Segment_Display u_7_segment_display_9 (
    .f(not_23_out), .a(not_23_out), .b(or_25_out), .e(not_23_out), .d(not_23_out), .c(or_26_out));  // open: g, dp
  or or_25 (or_25_out, not_23_out, xor_2_out);
  or or_26 (or_26_out, not_23_out, xor_2_out);

  // Notes on the sheet:
  //   operação
  //   Carry Out
  //   Borrow out
  //   BI
  //   CI
  //   Carry Out
  //   BI
  //   Borrow out
  //   CI
  //   Carry Out
  //   Borrow out
  //   BI
  //   CI
  //   overflow
  //   CI
  //   Carry Out
  //   BI
  //   Borrow out
  //   R3
  //   R2
  //   R1
  //   CARRY OUT 5 BIT
  //   BORROW OUT 5 BIT
  //   R0
endmodule

module teste (
  input  in_1
);

  wire not_1_out, or_1_out, or_2_out;

  not not_1 (not_1_out, in_1);
  _7_Segment_Display u_7_segment_display_1 (
    .f(not_1_out), .a(not_1_out), .b(or_2_out), .e(not_1_out), .d(not_1_out), .c(or_1_out));  // open: g, dp
  or or_1 (or_1_out, not_1_out, in_1);
  or or_2 (or_2_out, not_1_out, in_1);
endmodule
